# Fritzing sketch semaforo-com-botoeira (saved by Fritzing 0.9.2b)

parts:
  LED1 = LED - 5mm [color="Red (633nm)" package="5 mm [THT]"]
  LED2 = LED - 5mm [color="Yellow (592nm)" package="5 mm [THT]"]
  LED3 = LED - 5mm [color="Green (565nm)" package="5 mm [THT]"]
  R1 = Resistor [tolerance=±5% resistance=1k package="0805 [SMD]"]
  R2 = Resistor [tolerance=±5% resistance=1k package="0805 [SMD]"]
  Componente1 = Arduino Uno (Rev3) - ICSP
  R3 = Resistor [tolerance=±5% resistance=1k package="0603 [SMD]"]
  S1 = Momentary Switch [package=ksa_sealed_tac_switch]
  R4 = Resistor [tolerance=±5% resistance=10k package="0603 [SMD]"]

nets:
  N1: LED1.cathode, LED2.cathode, LED3.cathode, Componente1.GND, S1.4
  N2: LED1.anode, R1.Pin_0
  N3: LED2.anode, R2.Pin_0
  N4: LED3.anode, R3.Pin_0
  N5: R1.Pin_1, Componente1.D4
  N6: R2.Pin_1, Componente1.D3_PWM
  N7: Componente1.D2, R3.Pin_1
  N8: Componente1.D5_PWM, S1.2
  N9: Componente1.5V, R4.Pin_0
